# Fritzing sketch uPRWiring (saved by Fritzing 0.8.5b)

parts:
  U1 = uPR Micro Pulse Rifle Counter
  S1 = Toggle Switch [package=THT]
  BAT1 = BC9VPC [package=bc9vpc]
  S2 = Pushbutton [package=THT]
  S3 = Pushbutton [package=THT]

nets:
  N1: U1.GND, S2.leg1, S3.leg1
  N2: U1.B-, BAT1.V+
  N3: U1.B+, S1.L1
  N4: U1.TRIG, S2.leg0
  N5: U1.MAG, S3.leg0
  N6: S1.COM, BAT1.V-

custom parts:
  uPR Micro Pulse Rifle Counter: The smallest pulse rifle counter board available. Just counter, no sound.
