# Fritzing sketch InterfacingPowerLED (saved by Fritzing 0.8.5b)

parts:
  U1 = CAT4101 1A LED Driver
  U2 = uPR Micro Pulse Rifle Counter
  Power_RGB1 = Prolight RGB 3 Watt Star
  R1 = Resistor [tolerance=±5% resistance=680 package=THT]
  U3 = LIPO-2000mAh [package=lipo-2000]

nets:
  VCC: U1.Vcc, U2.Vcc
  N1: U1.EN/PWM, U2.SPARE1
  GND: U1.GND, U2.GND
  N2: U1.LED_Ground, U3.-
  N3: U1.LED_Cathode, Power_RGB1.B-
  N4: U1.Current_Set_1, R1.Pin_0
  N5: U1.Curent_Set_2, R1.Pin_1
  N6: Power_RGB1.R+, U3.+

custom parts:
  CAT4101 1A LED Driver: The CAT4101 can drive a high power LED (or chain of series linked LEDs) up to 1A. It also provides an Enable or PWM input pin for controlling the brightness of the LED through a low powered PWM signal from a microcontroller.
  uPR Micro Pulse Rifle Counter: The smallest pulse rifle counter board available. Just counter, no sound.
